# Fritzing sketch WifiThermometer (saved by Fritzing 0.9.3b)
circuit board: 8.46667cm x 5.64444cm
breadboards: 1

parts:
  DHT1 = DHT22 Humidity and Temperature Sensor
  Espessif_Serial_Wifi_Modul_1 = ESP8266 ESP01 [part_number=ESP8266 package=THT]
  USBTTL1 = USB TTL Serial Cable
  PSU1 = Adjustable Breadboard Power Supply
  R8 = Resistor [tolerance=±5% resistance=4.7k package="2010 [SMD]"]
  R7 = Resistor [tolerance=±5% resistance=330 package="2010 [SMD]"]
  S1 = Pushbutton [package="[SMD]"]
  S1-Program = Pushbutton [package="[SMD]"]
  R5 = Resistor [tolerance=±5% resistance=3.3k package="0805 [SMD]"]
  R4 = Resistor [tolerance=±5% resistance=3.3k package="0805 [SMD]"]
  R3 = Resistor [tolerance=±5% resistance=3.3k package="0805 [SMD]"]
  R2 = Resistor [tolerance=±5% resistance=3.3k package="0805 [SMD]"]
  R6 = Resistor [tolerance=±5% resistance=330 package="2010 [SMD]"]

nets:
  VDD: DHT1.VDD, Espessif_Serial_Wifi_Modul_1.VCC, USBTTL1.5V, PSU1.Vout+, R8.Pin_1, R5.Pin_1, R4.Pin_1, R3.Pin_1, R2.Pin_1
  N1: DHT1.DATA, R8.Pin_0
  N2: DHT1.NULL, Espessif_Serial_Wifi_Modul_1.GPIO02, R7.Pin_1, R3.Pin_0
  GND: DHT1.GND, Espessif_Serial_Wifi_Modul_1.GND, USBTTL1.GND, PSU1.Vout-, S1.Pin_1, S1.Pin_2, S1-Program.Pin_3, S1-Program.Pin_4
  N3: Espessif_Serial_Wifi_Modul_1.RXD, USBTTL1.RX
  N4: Espessif_Serial_Wifi_Modul_1.TXD, USBTTL1.TX
  N5: Espessif_Serial_Wifi_Modul_1.GPIO16, S1.Pin_3, S1.Pin_4, R5.Pin_0
  N6: Espessif_Serial_Wifi_Modul_1.GPIO00, S1-Program.Pin_1, S1-Program.Pin_2, R2.Pin_0, R6.Pin_1
  N7: Espessif_Serial_Wifi_Modul_1.CH_PD, R4.Pin_0

custom parts:
  ESP8266 ESP01: Generic WiFi Module based on the ESP8266 with onboard PCB antenna and UART communications
